# Fritzing sketch Light-Box Sketch 2 (saved by Fritzing 0.9.1b)
breadboards: 1

parts:
  Part1 = Arduino Mega 2560 (Rev3)
  S1 = Pushbutton [package="[THT]"]
  S2 = Pushbutton [package="[THT]"]
  S3 = Pushbutton [package="[THT]"]
  S4 = Pushbutton [package="[THT]"]
  R1 = Resistor [tolerance=±5% resistance=10k package=THT]
  R2 = Resistor [tolerance=±5% resistance=10k package=THT]
  R3 = Resistor [tolerance=±5% resistance=10k package=THT]
  R4 = Resistor [tolerance=±5% resistance=10k package=THT]

nets:
  N1: Part1.5V, S1.Pin_3, S1.Pin_4, S2.Pin_3, S2.Pin_4, S3.Pin_3, S3.Pin_4, S4.Pin_3, S4.Pin_4
  N2: Part1.GND, R1.Pin_0, R2.Pin_0, R3.Pin_0, R4.Pin_0
  N3: Part1.D22, S4.Pin_1, S4.Pin_2, R4.Pin_1
  N4: Part1.D24, S3.Pin_1, S3.Pin_2, R3.Pin_1
  N5: Part1.D26, S2.Pin_1, S2.Pin_2, R2.Pin_1
  N6: Part1.D28, S1.Pin_1, S1.Pin_2, R1.Pin_1
